// Logisim project 系统控制器.circ as structural Verilog: 1 circuit, main circuit main
module main (
  input  ena,
  input  rst,
  input  change,
  output out_4,
  output out_5,
  output out_6
);

  wire not_1_out, not_2_out, not_3_out;

  not not_1 (not_1_out, change);
  not not_2 (not_2_out, rst);
  not not_3 (not_3_out, ena);
  and and_1 (out_4, ena, rst);
  and and_2 (out_5, ena, not_1_out, not_2_out);
  and and_3 (out_6, change, not_2_out);
endmodule
